// Digital circuit Processador.dig as structural Verilog
module Processador (
  input  clk
);

  wire and_1_out, branch, halt, ip_mux, or_1_out, SelB, show, Write, zero;
  wire [2:0] op_ula;
  wire [3:0] Mem__Programa_d_2, Mem__Programa_d_3, Mem__Programa_d_4, opcode;
  wire [15:0] Mem__Programa_d;
  wire [23:0] d_ff_1_q, multiplexer_1_out, multiplexer_2_out, sinalext_24bit_1_out, SOMA_1_s;
  wire [31:0] flipflop_1_q, multiplexer_3_out, registrador32bit_1_a, registrador32bit_1_b, sinalext_1_out,
       ula_1_p4;

  Multiplexer #(.Bits(24)) multiplexer_1 (
    .sel(or_1_out), .in_0(24'h1), .in_1(sinalext_24bit_1_out), .out(multiplexer_1_out));
  or or_1 (or_1_out, ip_mux, and_1_out);
  Multiplexer #(.Bits(24)) multiplexer_2 (
    .sel(halt), .in_0(multiplexer_1_out), .in_1({24{1'b0}}), .out(multiplexer_2_out));
  and and_1 (and_1_out, zero, branch);
  ip SOMA_1 (.A(d_ff_1_q), .B(multiplexer_2_out), .S(SOMA_1_s));
  SinalEXt_24bit sinalext_24bit_1 (.In(Mem__Programa_d), .Out(sinalext_24bit_1_out));
  D_FF #(.Bits(24)) d_ff_1 (.D(SOMA_1_s), .C(clk), .Q(d_ff_1_q));  // open: nQ
  // Probe on d_ff_1_q
  ROM #(.AddrBits(24), .Bits(32)) Mem__Programa (
    .A(d_ff_1_q), .sel(1'b1),
    .D({opcode, Mem__Programa_d_4, Mem__Programa_d_3, Mem__Programa_d_2, Mem__Programa_d}));
  // Probe on {opcode, Mem__Programa_d_4, Mem__Programa_d_3, Mem__Programa_d_2, Mem__Programa_d}
  ROM #(.AddrBits(4), .Bits(9)) Mem__Controle (
    .A(opcode), .sel(1'b1), .D({Write, op_ula, branch, ip_mux, halt, SelB, show}));
  SinalEXt sinalext_1 (.In(Mem__Programa_d), .Out(sinalext_1_out));
  Registrador32bit registrador32bit_1 (
    .C(ula_1_p4), .a_2(Mem__Programa_d_4), .b_2(Mem__Programa_d_3), .c_2(Mem__Programa_d_2), .EN(Write),
    .clk(clk), .A(registrador32bit_1_a), .B(registrador32bit_1_b));
  Multiplexer #(.Bits(32)) multiplexer_3 (
    .sel(SelB), .in_0(registrador32bit_1_b), .in_1(sinalext_1_out), .out(multiplexer_3_out));
  Flipflop flipflop_1 (.D(registrador32bit_1_a), .clk(show), .Q(flipflop_1_q));
  // ULA ula_1: pin names not known; wires that end beside it: registrador32bit_1_a, multiplexer_3_out, op_ula, ula_1_p4, zero
  // Probe Show on flipflop_1_q

  // Notes on the sheet:
  //   contents of Mem__Programa (hex, n*v repeats v):
  //   0,b0010003,b0020002,11230000,c3000000
  //   contents of Mem__Controle (hex, n*v repeats v):
  //   0,100,120,140,352,180,1a0,1c0,1e0,162,182,102,1,8,138,c
endmodule
