// Digital circuit ULA.dig as structural Verilog
module ULA (
  input  [31:0] Alpha,
  input  [31:0] Beta,
  input  [2:0] fun,
  output [31:0] Gamma
);

  wire [31:0] somador_32bit_1_s;

  Somador_32bit somador_32bit_1 (.A(Alpha), .B(Beta), .S(somador_32bit_1_s));
  Multiplexer #(.Selector_Bits(3), .Bits(32)) multiplexer_1 (
    .sel(fun), .in_0(somador_32bit_1_s), .out(Gamma));  // open: in_1, in_2, in_3, in_4, in_5, in_6, in_7

  // Other names for the same wires on the sheet: A[31:0] = Alpha; B[31:0] = Beta
endmodule
